// Digital circuit C2.dig as structural Verilog
module C2 (
  input  [31:0] B,
  output [31:0] S
);

  wire add16_lsb_1_c_out, add16_msb_1_c_out, add16_msb_2_c_out;
  wire [15:0] add16_msb_1_s, add16_msb_2_s, not_1_out, not_1_out_2;

  assign {not_1_out_2, not_1_out} = ~B;  // Not not_1, 32 bits wide
  ADD16_LSB add16_lsb_1 (.B(16'h1), .A(not_1_out), .C_out(add16_lsb_1_c_out), .S(S[15:0]));
  ADD16_MSB add16_msb_1 (.B({16{1'b0}}), .A(not_1_out_2), .C_in(1'b0), .C_out(add16_msb_1_c_out), .S(add16_msb_1_s));
  ADD16_MSB add16_msb_2 (.B({16{1'b0}}), .A(not_1_out_2), .C_in(1'b1), .C_out(add16_msb_2_c_out), .S(add16_msb_2_s));
  LED led_1 (.in(add16_msb_1_c_out));
  LED led_2 (.in(add16_msb_2_c_out));
  Multiplexer #(.Bits(16)) multiplexer_1 (
    .sel(add16_lsb_1_c_out), .in_0(add16_msb_1_s), .in_1(add16_msb_2_s), .out(S[31:16]));
endmodule
