// Digital circuit AND.dig as structural Verilog
module AND (
  input  [31:0] E,
  input  [31:0] A,
  input  [31:0] B,
  output [31:0] S
);

  assign S = A & B & E;  // And and_1, 32 bits wide
endmodule
