// Digital circuit CPU.dig as structural Verilog
module CPU (
  input  [2:0] FUN
);

  wire add_2_p2, add_2_p3, ext_1_p1, multiplexer_1_out, reg_bank_1_p1, reg_bank_1_p2;
  wire [31:0] shift_1l_1_s, shift_1l_2_p2;

  // ADD add_1: pin names not known; wires that end beside it: 32'h3
  // REG_BANK reg_bank_1: pin names not known; wires that end beside it: reg_bank_1_p1, reg_bank_1_p2
  // EXT ext_1: pin names not known; wires that end beside it: ext_1_p1
  SHIFT_1L shift_1l_1 (.A(shift_1l_2_p2), .S(shift_1l_1_s));
  // SHIFT_1L shift_1l_2: pin names not known; wires that end beside it: ext_1_p1, shift_1l_2_p2
  Multiplexer multiplexer_1 (.in_0(reg_bank_1_p2), .in_1(ext_1_p1), .out(multiplexer_1_out));  // open: sel
  // ADD add_2: pin names not known; wires that end beside it: shift_1l_1_s, add_2_p2, add_2_p3
  ULA ula_1 (.A(reg_bank_1_p1), .B(multiplexer_1_out), .fun(FUN));
  LED led_1 (.in(add_2_p2));
  Multiplexer multiplexer_2 (.in_1(add_2_p3));  // open: sel, in_0, out
endmodule
