// Digital circuit NOT.dig as structural Verilog
module NOT (
  input  [31:0] A,
  input  [31:0] E,
  output [31:0] S
);

  wire and_1_out;

  and and_1 (and_1_out, A[0], E[0]);
  not not_1 (S[0], and_1_out);
  // Pins of 1 and 32 bits meet at A
  // Pins of 1 and 32 bits meet at E
  // Pins of 1 and 32 bits meet at S
endmodule
