// Digital circuit OR.dig as structural Verilog
module OR (
  input  [31:0] A,
  input  [31:0] B,
  input  [31:0] E,
  output [31:0] S
);

  wire [31:0] or_1_out;

  assign or_1_out = A | B;  // Or or_1, 32 bits wide
  assign S = E & or_1_out;  // And and_1, 32 bits wide
endmodule
