// Digital circuit REG.dig as structural Verilog
module REG (
  input  [31:0] D,
  input  CLK,
  input  E,
  output [31:0] S
);

  wire multiplexer_1_out, multiplexer_2_out, multiplexer_3_out, multiplexer_4_out, multiplexer_5_out,
       multiplexer_6_out, multiplexer_7_out, multiplexer_8_out, multiplexer_9_out, multiplexer_10_out,
       multiplexer_11_out, multiplexer_12_out, multiplexer_13_out, multiplexer_14_out, multiplexer_15_out,
       multiplexer_16_out, multiplexer_17_out, multiplexer_18_out, multiplexer_19_out, multiplexer_20_out,
       multiplexer_21_out, multiplexer_22_out, multiplexer_23_out, multiplexer_24_out, multiplexer_25_out,
       multiplexer_26_out, multiplexer_27_out, multiplexer_28_out, multiplexer_29_out, multiplexer_30_out,
       multiplexer_31_out, multiplexer_32_out;

  Multiplexer multiplexer_1 (.sel(E), .in_0(S[0]), .in_1(D[0]), .out(multiplexer_1_out));
  Multiplexer multiplexer_2 (.sel(E), .in_0(S[1]), .in_1(D[1]), .out(multiplexer_2_out));
  Multiplexer multiplexer_3 (.sel(E), .in_0(S[2]), .in_1(D[2]), .out(multiplexer_3_out));
  Multiplexer multiplexer_4 (.sel(E), .in_0(S[3]), .in_1(D[3]), .out(multiplexer_4_out));
  Multiplexer multiplexer_5 (.sel(E), .in_0(S[4]), .in_1(D[4]), .out(multiplexer_5_out));
  Multiplexer multiplexer_6 (.sel(E), .in_0(S[5]), .in_1(D[5]), .out(multiplexer_6_out));
  Multiplexer multiplexer_7 (.sel(E), .in_0(S[6]), .in_1(D[6]), .out(multiplexer_7_out));
  Multiplexer multiplexer_8 (.sel(E), .in_0(S[7]), .in_1(D[7]), .out(multiplexer_8_out));
  D_FF d_ff_1 (.D(multiplexer_1_out), .C(CLK), .Q(S[0]));  // open: nQ
  D_FF d_ff_2 (.D(multiplexer_2_out), .C(CLK), .Q(S[1]));  // open: nQ
  D_FF d_ff_3 (.D(multiplexer_3_out), .C(CLK), .Q(S[2]));  // open: nQ
  D_FF d_ff_4 (.D(multiplexer_4_out), .C(CLK), .Q(S[3]));  // open: nQ
  D_FF d_ff_5 (.D(multiplexer_5_out), .C(CLK), .Q(S[4]));  // open: nQ
  D_FF d_ff_6 (.D(multiplexer_6_out), .C(CLK), .Q(S[5]));  // open: nQ
  D_FF d_ff_7 (.D(multiplexer_7_out), .C(CLK), .Q(S[6]));  // open: nQ
  D_FF d_ff_8 (.D(multiplexer_8_out), .C(CLK), .Q(S[7]));  // open: nQ
  Multiplexer multiplexer_9 (.sel(E), .in_0(S[8]), .in_1(D[8]), .out(multiplexer_9_out));
  Multiplexer multiplexer_10 (.sel(E), .in_0(S[9]), .in_1(D[9]), .out(multiplexer_10_out));
  Multiplexer multiplexer_11 (.sel(E), .in_0(S[10]), .in_1(D[10]), .out(multiplexer_11_out));
  Multiplexer multiplexer_12 (.sel(E), .in_0(S[11]), .in_1(D[11]), .out(multiplexer_12_out));
  Multiplexer multiplexer_13 (.sel(E), .in_0(S[12]), .in_1(D[12]), .out(multiplexer_13_out));
  Multiplexer multiplexer_14 (.sel(E), .in_0(S[13]), .in_1(D[13]), .out(multiplexer_14_out));
  Multiplexer multiplexer_15 (.sel(E), .in_0(S[14]), .in_1(D[14]), .out(multiplexer_15_out));
  Multiplexer multiplexer_16 (.sel(E), .in_0(S[15]), .in_1(D[15]), .out(multiplexer_16_out));
  D_FF d_ff_9 (.D(multiplexer_9_out), .C(CLK), .Q(S[8]));  // open: nQ
  D_FF d_ff_10 (.D(multiplexer_10_out), .C(CLK), .Q(S[9]));  // open: nQ
  D_FF d_ff_11 (.D(multiplexer_11_out), .C(CLK), .Q(S[10]));  // open: nQ
  D_FF d_ff_12 (.D(multiplexer_12_out), .C(CLK), .Q(S[11]));  // open: nQ
  D_FF d_ff_13 (.D(multiplexer_13_out), .C(CLK), .Q(S[12]));  // open: nQ
  D_FF d_ff_14 (.D(multiplexer_14_out), .C(CLK), .Q(S[13]));  // open: nQ
  D_FF d_ff_15 (.D(multiplexer_15_out), .C(CLK), .Q(S[14]));  // open: nQ
  D_FF d_ff_16 (.D(multiplexer_16_out), .C(CLK), .Q(S[15]));  // open: nQ
  Multiplexer multiplexer_17 (.sel(E), .in_0(S[16]), .in_1(D[16]), .out(multiplexer_17_out));
  Multiplexer multiplexer_18 (.sel(E), .in_0(S[17]), .in_1(D[17]), .out(multiplexer_18_out));
  Multiplexer multiplexer_19 (.sel(E), .in_0(S[18]), .in_1(D[18]), .out(multiplexer_19_out));
  Multiplexer multiplexer_20 (.sel(E), .in_0(S[19]), .in_1(D[19]), .out(multiplexer_20_out));
  Multiplexer multiplexer_21 (.sel(E), .in_0(S[20]), .in_1(D[20]), .out(multiplexer_21_out));
  Multiplexer multiplexer_22 (.sel(E), .in_0(S[21]), .in_1(D[21]), .out(multiplexer_22_out));
  Multiplexer multiplexer_23 (.sel(E), .in_0(S[22]), .in_1(D[22]), .out(multiplexer_23_out));
  Multiplexer multiplexer_24 (.sel(E), .in_0(S[23]), .in_1(D[23]), .out(multiplexer_24_out));
  D_FF d_ff_17 (.D(multiplexer_17_out), .C(CLK), .Q(S[16]));  // open: nQ
  D_FF d_ff_18 (.D(multiplexer_18_out), .C(CLK), .Q(S[17]));  // open: nQ
  D_FF d_ff_19 (.D(multiplexer_19_out), .C(CLK), .Q(S[18]));  // open: nQ
  D_FF d_ff_20 (.D(multiplexer_20_out), .C(CLK), .Q(S[19]));  // open: nQ
  D_FF d_ff_21 (.D(multiplexer_21_out), .C(CLK), .Q(S[20]));  // open: nQ
  D_FF d_ff_22 (.D(multiplexer_22_out), .C(CLK), .Q(S[21]));  // open: nQ
  D_FF d_ff_23 (.D(multiplexer_23_out), .C(CLK), .Q(S[22]));  // open: nQ
  D_FF d_ff_24 (.D(multiplexer_24_out), .C(CLK), .Q(S[23]));  // open: nQ
  Multiplexer multiplexer_25 (.sel(E), .in_0(S[24]), .in_1(D[24]), .out(multiplexer_25_out));
  Multiplexer multiplexer_26 (.sel(E), .in_0(S[25]), .in_1(D[25]), .out(multiplexer_26_out));
  Multiplexer multiplexer_27 (.sel(E), .in_0(S[26]), .in_1(D[26]), .out(multiplexer_27_out));
  Multiplexer multiplexer_28 (.sel(E), .in_0(S[27]), .in_1(D[27]), .out(multiplexer_28_out));
  Multiplexer multiplexer_29 (.sel(E), .in_0(S[28]), .in_1(D[28]), .out(multiplexer_29_out));
  Multiplexer multiplexer_30 (.sel(E), .in_0(S[29]), .in_1(D[29]), .out(multiplexer_30_out));
  Multiplexer multiplexer_31 (.sel(E), .in_0(S[30]), .in_1(D[30]), .out(multiplexer_31_out));
  Multiplexer multiplexer_32 (.sel(E), .in_0(S[31]), .in_1(D[31]), .out(multiplexer_32_out));
  D_FF d_ff_25 (.D(multiplexer_25_out), .C(CLK), .Q(S[24]));  // open: nQ
  D_FF d_ff_26 (.D(multiplexer_26_out), .C(CLK), .Q(S[25]));  // open: nQ
  D_FF d_ff_27 (.D(multiplexer_27_out), .C(CLK), .Q(S[26]));  // open: nQ
  D_FF d_ff_28 (.D(multiplexer_28_out), .C(CLK), .Q(S[27]));  // open: nQ
  D_FF d_ff_29 (.D(multiplexer_29_out), .C(CLK), .Q(S[28]));  // open: nQ
  D_FF d_ff_30 (.D(multiplexer_30_out), .C(CLK), .Q(S[29]));  // open: nQ
  D_FF d_ff_31 (.D(multiplexer_31_out), .C(CLK), .Q(S[30]));  // open: nQ
  D_FF d_ff_32 (.D(multiplexer_32_out), .C(CLK), .Q(S[31]));  // open: nQ

  // Other names for the same wires on the sheet: T_0 = D[8]; T_1 = D[9]; T_2 = D[10]; T_3 = D[11]; T_4 = D[12];
  //   T_5 = D[13]; T_6 = D[14]; T_7 = D[15]; T_8 = D[16]; T_9 = D[17]; T_10 = D[18]; T_11 = D[19]; T_12 = D[20];
  //   T_13 = D[21]; T_14 = D[22]; T_15 = D[23]; T_16 = D[24]; T_17 = D[25]; T_18 = D[26]; T_19 = D[27]; T_20 = D[28];
  //   T_21 = D[29]; T_22 = D[30]; T_23 = D[31]; S_0 = S[0]; S_1 = S[1]; S_2 = S[2]; S_3 = S[3]; S_4 = S[4];
  //   S_5 = S[5]; S_6 = S[6]; S_7 = S[7]; S_8 = S[8]; S_9 = S[9]; S_10 = S[10]; S_11 = S[11]; S_12 = S[12];
  //   S_13 = S[13]; S_14 = S[14]; S_15 = S[15]; S_16 = S[16]; S_17 = S[17]; S_18 = S[18]; S_19 = S[19]; S_20 = S[20];
  //   S_21 = S[21]; S_22 = S[22]; S_23 = S[23]; S_24 = S[24]; S_25 = S[25]; S_26 = S[26]; S_27 = S[27]; S_28 = S[28];
  //   S_29 = S[29]; S_30 = S[30]; S_31 = S[31]

  // Notes on the sheet:
  //   CLK: Hz: 5
endmodule
