// Digital circuit REG_BANK.dig as structural Verilog
module REG_BANK (
  input  [31:0] W,
  input  [3:0] END_W,
  input  [3:0] END_A,
  input  CLK,
  input  [3:0] END_B,
  output [31:0] A,
  output [31:0] B
);

  wire E_0, E_1, E_2, E_3, E_4, E_5, E_6, E_7, E_8, E_9, E_10, E_11, E_12, E_13, E_14, E_15;
  wire [31:0] and_1_out, and_2_out, R_0, R_1, R_2, R_3, R_4, R_5, R_6, R_7, R_8, R_9, R_10, R_11, R_12, R_13,
       R_14, R_15, W_0, W_1, W_2, W_3, W_4, W_5, W_6, W_7, W_8, W_9, W_10, W_11, W_12, W_13, W_14, W_15;

  Demultiplexer #(.Selector_Bits(4), .Bits(32)) demultiplexer_1 (
    .sel(END_W), .in(W), .out_0(W_0), .out_1(W_1), .out_2(W_2), .out_3(W_3), .out_4(W_4), .out_5(W_5),
    .out_6(W_6), .out_7(W_7), .out_8(W_8), .out_9(W_9), .out_10(W_10), .out_11(W_11), .out_12(W_12),
    .out_13(W_13), .out_14(W_14), .out_15(W_15));
  Decoder #(.Selector_Bits(4)) decoder_1 (
    .sel(END_W), .out_0(E_0), .out_1(E_1), .out_2(E_2), .out_3(E_3), .out_4(E_4), .out_5(E_5), .out_6(E_6),
    .out_7(E_7), .out_8(E_8), .out_9(E_9), .out_10(E_10), .out_11(E_11), .out_12(E_12), .out_13(E_13),
    .out_14(E_14), .out_15(E_15));
  REG reg_1 (.D(W_0), .CLK(CLK), .E(E_0), .S(R_0));
  REG reg_2 (.D(W_1), .CLK(CLK), .E(E_1), .S(R_1));
  REG reg_3 (.D(W_2), .CLK(CLK), .E(E_2), .S(R_2));
  REG reg_4 (.D(W_3), .CLK(CLK), .E(E_3), .S(R_3));
  REG reg_5 (.D(W_4), .CLK(CLK), .E(E_4), .S(R_4));
  REG reg_6 (.D(W_5), .CLK(CLK), .E(E_5), .S(R_5));
  REG reg_7 (.D(W_6), .CLK(CLK), .E(E_6), .S(R_6));
  REG reg_8 (.D(W_7), .CLK(CLK), .E(E_7), .S(R_7));
  REG reg_9 (.D(W_8), .CLK(CLK), .E(E_8), .S(R_8));
  REG reg_10 (.D(W_9), .CLK(CLK), .E(E_9), .S(R_9));
  REG reg_11 (.D(W_10), .CLK(CLK), .E(E_10), .S(R_10));
  REG reg_12 (.D(W_11), .CLK(CLK), .E(E_11), .S(R_11));
  REG reg_13 (.D(W_12), .CLK(CLK), .E(E_12), .S(R_12));
  REG reg_14 (.D(W_13), .CLK(CLK), .E(E_13), .S(R_13));
  REG reg_15 (.D(W_14), .CLK(CLK), .E(E_14), .S(R_14));
  REG reg_16 (.D(W_15), .CLK(CLK), .E(E_15), .S(R_15));
  assign and_1_out = {32{1'b0}} & R_0;  // And and_1, 32 bits wide
  assign and_2_out = {32{1'b0}} & R_0;  // And and_2, 32 bits wide
  Multiplexer #(.Selector_Bits(4), .Bits(32)) multiplexer_1 (
    .sel(END_A), .in_0(and_1_out), .in_1(R_1), .in_2(R_2), .in_3(R_3), .in_4(R_4), .in_5(R_5), .in_6(R_6),
    .in_7(R_7), .in_8(R_8), .in_9(R_9), .in_10(R_10), .in_11(R_11), .in_12(R_12), .in_13(R_13), .in_14(R_14),
    .in_15(R_15), .out(A));
  Multiplexer #(.Selector_Bits(4), .Bits(32)) multiplexer_2 (
    .sel(END_B), .in_0(and_2_out), .in_1(R_1), .in_2(R_2), .in_3(R_3), .in_4(R_4), .in_5(R_5), .in_6(R_6),
    .in_7(R_7), .in_8(R_8), .in_9(R_9), .in_10(R_10), .in_11(R_11), .in_12(R_12), .in_13(R_13), .in_14(R_14),
    .in_15(R_15), .out(B));

  // Notes on the sheet:
  //   CLK: Hz: 5
endmodule
