// Digital circuit ULA.dig as structural Verilog
module ULA (
  input  [31:0] A,
  input  [31:0] B,
  input  [2:0] fun
);

  NOT not_1 (.A(A));  // open: S
  XOR xor_1 (.A(A), .B(B));  // open: S
  OR or_1 (.A(A), .B(B));  // open: S
  Multiplexer #(.Bits(32), .Selector_Bits(3)) multiplexer_1 (.sel(fun));  // open: in_0, in_1, in_2, in_3, in_4, in_5, in_6, in_7, out
  AND and_1 (.A(A), .B(B));  // open: S
  // Pins of 1 and 32 bits meet at A
  // Pins of 1 and 32 bits meet at B
endmodule
