// Digital circuit ADD.dig as structural Verilog
module ADD (
  input  [31:0] A,
  input  [31:0] B,
  output [31:0] S
);

  wire add16_lsb_1_c_out, add16_msb_1_c_out, add16_msb_2_c_out;
  wire [15:0] add16_msb_1_s, add16_msb_2_s;

  ADD16_LSB add16_lsb_1 (.B(B[15:0]), .A(A[15:0]), .C_out(add16_lsb_1_c_out), .S(S[15:0]));
  ADD16_MSB add16_msb_1 (.B(B[31:16]), .A(A[31:16]), .C_in(1'b0), .C_out(add16_msb_1_c_out), .S(add16_msb_1_s));
  ADD16_MSB add16_msb_2 (.B(B[31:16]), .A(A[31:16]), .C_in(1'b1), .C_out(add16_msb_2_c_out), .S(add16_msb_2_s));
  LED led_1 (.in(add16_msb_1_c_out));
  LED led_2 (.in(add16_msb_2_c_out));
  Multiplexer #(.Bits(16)) multiplexer_1 (
    .sel(add16_lsb_1_c_out), .in_0(add16_msb_1_s), .in_1(add16_msb_2_s), .out(S[31:16]));
endmodule
