// Digital circuit ADD16_MSB.dig as structural Verilog
module ADD16_MSB (
  input  [15:0] B,
  input  [15:0] A,
  input  C_in,
  output C_out,
  output [15:0] S
);

  wire fadder_2_c_out, fadder_3_c_out, fadder_4_c_out, fadder_5_c_out, fadder_6_c_out, fadder_7_c_out,
       fadder_8_c_out, fadder_9_c_out, fadder_10_c_out, fadder_11_c_out, fadder_12_c_out, fadder_13_c_out,
       fadder_14_c_out, fadder_15_c_out, fadder_16_c_out;

  fAdder fadder_1 (.A(B[15]), .B(A[15]), .C_in(fadder_2_c_out), .S(S[15]), .C_out(C_out));
  fAdder fadder_2 (.A(B[14]), .B(A[14]), .C_in(fadder_3_c_out), .S(S[14]), .C_out(fadder_2_c_out));
  fAdder fadder_3 (.A(B[13]), .B(A[13]), .C_in(fadder_4_c_out), .S(S[13]), .C_out(fadder_3_c_out));
  fAdder fadder_4 (.A(B[12]), .B(A[12]), .C_in(fadder_5_c_out), .S(S[12]), .C_out(fadder_4_c_out));
  fAdder fadder_5 (.A(B[11]), .B(A[11]), .C_in(fadder_6_c_out), .S(S[11]), .C_out(fadder_5_c_out));
  fAdder fadder_6 (.A(B[10]), .B(A[10]), .C_in(fadder_7_c_out), .S(S[10]), .C_out(fadder_6_c_out));
  fAdder fadder_7 (.A(B[9]), .B(A[9]), .C_in(fadder_8_c_out), .S(S[9]), .C_out(fadder_7_c_out));
  fAdder fadder_8 (.A(B[8]), .B(A[8]), .C_in(fadder_9_c_out), .S(S[8]), .C_out(fadder_8_c_out));
  fAdder fadder_9 (.A(B[7]), .B(A[7]), .C_in(fadder_10_c_out), .S(S[7]), .C_out(fadder_9_c_out));
  fAdder fadder_10 (.A(B[6]), .B(A[6]), .C_in(fadder_11_c_out), .S(S[6]), .C_out(fadder_10_c_out));
  fAdder fadder_11 (.A(B[5]), .B(A[5]), .C_in(fadder_12_c_out), .S(S[5]), .C_out(fadder_11_c_out));
  fAdder fadder_12 (.A(B[4]), .B(A[4]), .C_in(fadder_13_c_out), .S(S[4]), .C_out(fadder_12_c_out));
  fAdder fadder_13 (.A(B[3]), .B(A[3]), .C_in(fadder_14_c_out), .S(S[3]), .C_out(fadder_13_c_out));
  fAdder fadder_14 (.A(B[2]), .B(A[2]), .C_in(fadder_15_c_out), .S(S[2]), .C_out(fadder_14_c_out));
  fAdder fadder_15 (.A(B[1]), .B(A[1]), .C_in(fadder_16_c_out), .S(S[1]), .C_out(fadder_15_c_out));
  fAdder fadder_16 (.A(B[0]), .B(A[0]), .C_in(C_in), .S(S[0]), .C_out(fadder_16_c_out));
endmodule
