// Digital circuit SHIFT_1R.dig as structural Verilog
module SHIFT_1R (
  input  [31:0] A,
  output [31:0] S
);

  LED led_1 (.in(A[0]));

  assign S = {1'b0, A[31:1]};

  // Other names for the same wires on the sheet: S_1 = A[1]; S_2 = A[2]; S_3 = A[3]; S_4 = A[4]; S_5 = A[5];
  //   S_6 = A[6]; S_7 = A[7]; S_8 = A[8]; S_9 = A[9]; S_10 = A[10]; S_11 = A[11]; S_12 = A[12]; S_13 = A[13];
  //   S_14 = A[14]; S_15 = A[15]; S_16 = A[16]; S_17 = A[17]; S_18 = A[18]; S_19 = A[19]; S_20 = A[20]; S_21 = A[21];
  //   S_22 = A[22]; S_23 = A[23]; S_24 = A[24]; S_25 = A[25]; S_26 = A[26]; S_27 = A[27]; S_28 = A[28]; S_29 = A[29];
  //   S_30 = A[30]; S_31 = A[31]
endmodule
