// Digital circuit SLL.dig as structural Verilog
module SLL (
  input  [31:0] A,
  input  [31:0] B,
  output [31:0] S
);

  wire [31:0] shift_1l_1_s, shift_1l_2_s, shift_1l_3_s, shift_1l_4_s, shift_1l_5_s, shift_1l_6_s,
       shift_1l_7_s, shift_1l_8_s, shift_1l_9_s, shift_1l_10_s, shift_1l_11_s, shift_1l_12_s, shift_1l_13_s,
       shift_1l_14_s, shift_1l_15_s, shift_1l_16_s, shift_1l_17_s, shift_1l_18_s, shift_1l_19_s,
       shift_1l_20_s, shift_1l_21_s, shift_1l_22_s, shift_1l_23_s, shift_1l_24_s, shift_1l_25_s,
       shift_1l_26_s, shift_1l_27_s, shift_1l_28_s, shift_1l_29_s, shift_1l_30_s, shift_1l_31_s;

  SHIFT_1L shift_1l_1 (.A(A), .S(shift_1l_1_s));
  SHIFT_1L shift_1l_2 (.A(shift_1l_1_s), .S(shift_1l_2_s));
  SHIFT_1L shift_1l_3 (.A(shift_1l_2_s), .S(shift_1l_3_s));
  SHIFT_1L shift_1l_4 (.A(shift_1l_3_s), .S(shift_1l_4_s));
  SHIFT_1L shift_1l_5 (.A(shift_1l_4_s), .S(shift_1l_5_s));
  SHIFT_1L shift_1l_6 (.A(shift_1l_5_s), .S(shift_1l_6_s));
  SHIFT_1L shift_1l_7 (.A(shift_1l_6_s), .S(shift_1l_7_s));
  SHIFT_1L shift_1l_8 (.A(shift_1l_7_s), .S(shift_1l_8_s));
  SHIFT_1L shift_1l_9 (.A(shift_1l_8_s), .S(shift_1l_9_s));
  SHIFT_1L shift_1l_10 (.A(shift_1l_9_s), .S(shift_1l_10_s));
  SHIFT_1L shift_1l_11 (.A(shift_1l_10_s), .S(shift_1l_11_s));
  SHIFT_1L shift_1l_12 (.A(shift_1l_11_s), .S(shift_1l_12_s));
  SHIFT_1L shift_1l_13 (.A(shift_1l_12_s), .S(shift_1l_13_s));
  SHIFT_1L shift_1l_14 (.A(shift_1l_13_s), .S(shift_1l_14_s));
  SHIFT_1L shift_1l_15 (.A(shift_1l_14_s), .S(shift_1l_15_s));
  SHIFT_1L shift_1l_16 (.A(shift_1l_15_s), .S(shift_1l_16_s));
  SHIFT_1L shift_1l_17 (.A(shift_1l_16_s), .S(shift_1l_17_s));
  SHIFT_1L shift_1l_18 (.A(shift_1l_17_s), .S(shift_1l_18_s));
  SHIFT_1L shift_1l_19 (.A(shift_1l_18_s), .S(shift_1l_19_s));
  SHIFT_1L shift_1l_20 (.A(shift_1l_19_s), .S(shift_1l_20_s));
  SHIFT_1L shift_1l_21 (.A(shift_1l_20_s), .S(shift_1l_21_s));
  SHIFT_1L shift_1l_22 (.A(shift_1l_21_s), .S(shift_1l_22_s));
  SHIFT_1L shift_1l_23 (.A(shift_1l_22_s), .S(shift_1l_23_s));
  SHIFT_1L shift_1l_24 (.A(shift_1l_23_s), .S(shift_1l_24_s));
  SHIFT_1L shift_1l_25 (.A(shift_1l_24_s), .S(shift_1l_25_s));
  SHIFT_1L shift_1l_26 (.A(shift_1l_25_s), .S(shift_1l_26_s));
  SHIFT_1L shift_1l_27 (.A(shift_1l_26_s), .S(shift_1l_27_s));
  SHIFT_1L shift_1l_28 (.A(shift_1l_27_s), .S(shift_1l_28_s));
  SHIFT_1L shift_1l_29 (.A(shift_1l_28_s), .S(shift_1l_29_s));
  SHIFT_1L shift_1l_30 (.A(shift_1l_29_s), .S(shift_1l_30_s));
  SHIFT_1L shift_1l_31 (.A(shift_1l_30_s), .S(shift_1l_31_s));
  Multiplexer #(.Selector_Bits(5), .Bits(32)) multiplexer_1 (
    .sel(B[4:0]), .in_0(A), .in_1(shift_1l_1_s), .in_2(shift_1l_2_s), .in_3(shift_1l_3_s),
    .in_4(shift_1l_4_s), .in_5(shift_1l_5_s), .in_6(shift_1l_6_s), .in_7(shift_1l_7_s), .in_8(shift_1l_8_s),
    .in_9(shift_1l_9_s), .in_10(shift_1l_10_s), .in_11(shift_1l_11_s), .in_12(shift_1l_12_s),
    .in_13(shift_1l_13_s), .in_14(shift_1l_14_s), .in_15(shift_1l_15_s), .in_16(shift_1l_16_s),
    .in_17(shift_1l_17_s), .in_18(shift_1l_18_s), .in_19(shift_1l_19_s), .in_20(shift_1l_20_s),
    .in_21(shift_1l_21_s), .in_22(shift_1l_22_s), .in_23(shift_1l_23_s), .in_24(shift_1l_24_s),
    .in_25(shift_1l_25_s), .in_26(shift_1l_26_s), .in_27(shift_1l_27_s), .in_28(shift_1l_28_s),
    .in_29(shift_1l_29_s), .in_30(shift_1l_30_s), .in_31(shift_1l_31_s), .out(S));
endmodule
