// Digital circuit SRL.dig as structural Verilog
module SRL (
  input  [31:0] A,
  input  [31:0] B,
  output [31:0] S
);

  wire [31:0] shift_1r_1_s, shift_1r_2_s, shift_1r_3_s, shift_1r_4_s, shift_1r_5_s, shift_1r_6_s,
       shift_1r_7_s, shift_1r_8_s, shift_1r_9_s, shift_1r_10_s, shift_1r_11_s, shift_1r_12_s, shift_1r_13_s,
       shift_1r_14_s, shift_1r_15_s, shift_1r_16_s, shift_1r_17_s, shift_1r_18_s, shift_1r_19_s,
       shift_1r_20_s, shift_1r_21_s, shift_1r_22_s, shift_1r_23_s, shift_1r_24_s, shift_1r_25_s,
       shift_1r_26_s, shift_1r_27_s, shift_1r_28_s, shift_1r_29_s, shift_1r_30_s, shift_1r_31_s;

  SHIFT_1R shift_1r_1 (.A(A), .S(shift_1r_1_s));
  SHIFT_1R shift_1r_2 (.A(shift_1r_1_s), .S(shift_1r_2_s));
  SHIFT_1R shift_1r_3 (.A(shift_1r_2_s), .S(shift_1r_3_s));
  SHIFT_1R shift_1r_4 (.A(shift_1r_3_s), .S(shift_1r_4_s));
  SHIFT_1R shift_1r_5 (.A(shift_1r_4_s), .S(shift_1r_5_s));
  SHIFT_1R shift_1r_6 (.A(shift_1r_5_s), .S(shift_1r_6_s));
  SHIFT_1R shift_1r_7 (.A(shift_1r_6_s), .S(shift_1r_7_s));
  SHIFT_1R shift_1r_8 (.A(shift_1r_7_s), .S(shift_1r_8_s));
  SHIFT_1R shift_1r_9 (.A(shift_1r_8_s), .S(shift_1r_9_s));
  SHIFT_1R shift_1r_10 (.A(shift_1r_9_s), .S(shift_1r_10_s));
  SHIFT_1R shift_1r_11 (.A(shift_1r_10_s), .S(shift_1r_11_s));
  SHIFT_1R shift_1r_12 (.A(shift_1r_11_s), .S(shift_1r_12_s));
  SHIFT_1R shift_1r_13 (.A(shift_1r_12_s), .S(shift_1r_13_s));
  SHIFT_1R shift_1r_14 (.A(shift_1r_13_s), .S(shift_1r_14_s));
  SHIFT_1R shift_1r_15 (.A(shift_1r_14_s), .S(shift_1r_15_s));
  SHIFT_1R shift_1r_16 (.A(shift_1r_15_s), .S(shift_1r_16_s));
  SHIFT_1R shift_1r_17 (.A(shift_1r_16_s), .S(shift_1r_17_s));
  SHIFT_1R shift_1r_18 (.A(shift_1r_17_s), .S(shift_1r_18_s));
  SHIFT_1R shift_1r_19 (.A(shift_1r_18_s), .S(shift_1r_19_s));
  SHIFT_1R shift_1r_20 (.A(shift_1r_19_s), .S(shift_1r_20_s));
  SHIFT_1R shift_1r_21 (.A(shift_1r_20_s), .S(shift_1r_21_s));
  SHIFT_1R shift_1r_22 (.A(shift_1r_21_s), .S(shift_1r_22_s));
  SHIFT_1R shift_1r_23 (.A(shift_1r_22_s), .S(shift_1r_23_s));
  SHIFT_1R shift_1r_24 (.A(shift_1r_23_s), .S(shift_1r_24_s));
  SHIFT_1R shift_1r_25 (.A(shift_1r_24_s), .S(shift_1r_25_s));
  SHIFT_1R shift_1r_26 (.A(shift_1r_25_s), .S(shift_1r_26_s));
  SHIFT_1R shift_1r_27 (.A(shift_1r_26_s), .S(shift_1r_27_s));
  SHIFT_1R shift_1r_28 (.A(shift_1r_27_s), .S(shift_1r_28_s));
  SHIFT_1R shift_1r_29 (.A(shift_1r_28_s), .S(shift_1r_29_s));
  SHIFT_1R shift_1r_30 (.A(shift_1r_29_s), .S(shift_1r_30_s));
  SHIFT_1R shift_1r_31 (.A(shift_1r_30_s), .S(shift_1r_31_s));
  Multiplexer #(.Selector_Bits(5), .Bits(32)) multiplexer_1 (
    .sel(B[4:0]), .in_0(A), .in_1(shift_1r_1_s), .in_2(shift_1r_2_s), .in_3(shift_1r_3_s),
    .in_4(shift_1r_4_s), .in_5(shift_1r_5_s), .in_6(shift_1r_6_s), .in_7(shift_1r_7_s), .in_8(shift_1r_8_s),
    .in_9(shift_1r_9_s), .in_10(shift_1r_10_s), .in_11(shift_1r_11_s), .in_12(shift_1r_12_s),
    .in_13(shift_1r_13_s), .in_14(shift_1r_14_s), .in_15(shift_1r_15_s), .in_16(shift_1r_16_s),
    .in_17(shift_1r_17_s), .in_18(shift_1r_18_s), .in_19(shift_1r_19_s), .in_20(shift_1r_20_s),
    .in_21(shift_1r_21_s), .in_22(shift_1r_22_s), .in_23(shift_1r_23_s), .in_24(shift_1r_24_s),
    .in_25(shift_1r_25_s), .in_26(shift_1r_26_s), .in_27(shift_1r_27_s), .in_28(shift_1r_28_s),
    .in_29(shift_1r_29_s), .in_30(shift_1r_30_s), .in_31(shift_1r_31_s), .out(S));
endmodule
