// Digital circuit ULA.dig as structural Verilog
module ULA (
  input  [31:0] A,
  input  [31:0] B,
  input  [2:0] fun,
  output [31:0] S,
  output ZERO
);

  wire and_2_out, and_3_out, and_4_out, and_5_out, and_6_out, and_7_out, and_8_out, and_9_out, and_10_out,
       and_11_out;
  wire [31:0] add_1_s, and_1_s, not_1_s, or_1_s, sll_1_s, srl_1_s, sub_1_s, xor_1_s;

  SRL srl_1 (.A(A), .B(B), .S(srl_1_s));
  SLL sll_1 (.A(A), .B(B), .S(sll_1_s));
  NOT not_1 (.A(A), .S(not_1_s));
  XOR xor_1 (.A(A), .B(B), .S(xor_1_s));
  OR or_1 (.A(A), .B(B), .S(or_1_s));
  Multiplexer #(.Selector_Bits(3), .Bits(32)) multiplexer_1 (
    .sel(fun), .in_0(add_1_s), .in_1(sub_1_s), .in_2(and_1_s), .in_3(or_1_s), .in_4(xor_1_s), .in_5(not_1_s),
    .in_6(sll_1_s), .in_7(srl_1_s), .out(S));
  AND and_1 (.A(A), .B(B), .S(and_1_s));
  SUB sub_1 (.A(A), .B(B), .S(sub_1_s));
  ADD add_1 (.A(A), .B(B), .S(add_1_s));
  and and_2 (and_2_out, ~S[0], ~S[1], ~S[2], ~S[3]);  // And
  and and_3 (and_3_out, ~S[4], ~S[5], ~S[6], ~S[7]);  // And
  and and_4 (and_4_out, ~S[8], ~S[9], ~S[10], ~S[11]);  // And
  and and_5 (and_5_out, ~S[12], ~S[13], ~S[14], ~S[15]);  // And
  and and_6 (and_6_out, ~S[16], ~S[17], ~S[18], ~S[19]);  // And
  and and_7 (and_7_out, ~S[20], ~S[21], ~S[22], ~S[23]);  // And
  and and_8 (and_8_out, ~S[24], ~S[25], ~S[26], ~S[27]);  // And
  and and_9 (and_9_out, ~S[28], ~S[29], ~S[30], ~S[31]);  // And
  and and_10 (and_10_out, and_2_out, and_3_out, and_4_out, and_5_out);
  and and_11 (and_11_out, and_6_out, and_7_out, and_8_out, and_9_out);
  and and_12 (ZERO, and_10_out, and_11_out);
endmodule
