// Digital circuit fAdder.dig as structural Verilog
module fAdder (
  input  A,
  input  B,
  input  C_in,
  output S,
  output C_out
);

  wire and_1_out, and_2_out, and_3_out, or_1_out, xor_1_out;

  xor xor_1 (xor_1_out, A, B);
  xor xor_2 (S, xor_1_out, C_in);
  and and_1 (and_1_out, A, B);
  and and_2 (and_2_out, B, C_in);
  or or_1 (or_1_out, and_1_out, and_2_out);
  and and_3 (and_3_out, A, C_in);
  or or_2 (C_out, or_1_out, and_3_out);
endmodule
