// Digital circuit XOR.dig as structural Verilog
module XOR (
  input  [31:0] E,
  input  [31:0] A,
  input  [31:0] B,
  output [31:0] S
);

  wire [31:0] xor_1_out;

  assign xor_1_out = A ^ B;  // XOr xor_1, 32 bits wide
  assign S = E & xor_1_out;  // And and_1, 32 bits wide
endmodule
